# Fritzing sketch Pito_con_led (saved by Fritzing 0.8.7b)
breadboards: 1

parts:
  U1 = attiny85 [package=dip]
  S1 = Pushbutton [package="[THT]"]
  BAT1 = Battery Holders [package=battcom_20mm_pth]
  BAT2 = Battery Holders [package=battcom_20mm_pth]
  J1 = Piezo Speaker
  LED1 = RGB LED (com. anode, rbg) [package="5 mm [THT]"]
  C1 = Electrolytic Capacitor [capacitance=10µF package="1010 [SMD, electrolytic]"]  # not connected
  R1 = Resistor [tolerance=±5% resistance=330 package=THT]
  R2 = Resistor [tolerance=±5% resistance=330 package=THT]
  R3 = Resistor [tolerance=±5% resistance=330 package=THT]
  R4 = Resistor [tolerance=±5% resistance=10k package=THT]

nets:
  N1: U1.Pin_2, S1.Pin_1, S1.Pin_2, R4.Pin_0
  N2: U1.Pin_3, J1.pin2
  N3: U1.Pin_4, BAT2.-, J1.pin1, LED1.common_anode, R4.Pin_1
  N4: U1.Pin_5, R3.Pin_1
  N5: U1.Pin_6, R2.Pin_0
  N6: U1.Pin_7, R1.Pin_0
  N7: U1.Pin_8, S1.Pin_3, S1.Pin_4, BAT1.+
  N8: BAT1.-, BAT2.+
  N9: LED1.red_cathode, R3.Pin_0
  N10: LED1.blue_cathode, R2.Pin_1
  N11: LED1.green_cathode, R1.Pin_1
