# Fritzing sketch giratorio (saved by Fritzing 0.9.1b)
breadboards: 1

parts:
  Part1 = Arduino Uno (Rev3) - ICSP
  Q1 = TRANSISTOR_PNP [package=to-92]
  R1 = Resistor [tolerance=±5% resistance=330 package="0603 [SMD]"]
  M1 = DC Motor
  D1 = Zener Diode [part_number=1N4732A breakdown_voltage=3.6V package="Melf DO-213 AB [SMD]"]
  C1 = Electrolytic Capacitor [capacitance=1μF voltage=20V package="0405 [SMD, electrolytic]"]

nets:
  N1: Part1.D3_PWM, R1.Pin_1
  N2: Part1.5V, M1.pin_1, D1.cathode, C1.+
  N3: Part1.GND, Q1.C
  N4: Q1.E, M1.pin_2, D1.anode, C1.-
  N5: Q1.B, R1.Pin_0
