# Fritzing sketch luces_arbolito (saved by Fritzing 0.8.7b)
breadboards: 1

parts:
  C1 = Electrolytic Capacitor [capacitance=10μF voltage=35V package="0605 [SMD, electrolytic]"]
  U1 = attiny85 [package=dip]
  LED2 = LED - 3mm [color="White (4500K)" package="3 mm [THT]"]
  LED3 = LED - 3mm [color="White (4500K)" package="3 mm [THT]"]
  LED4 = LED - 3mm [color="White (4500K)" package="3 mm [THT]"]
  LED5 = LED - 3mm [color="White (4500K)" package="3 mm [THT]"]
  LED6 = LED - 3mm [color="White (4500K)" package="3 mm [THT]"]
  LED7 = LED - 3mm [color="White (4500K)" package="3 mm [THT]"]
  VCC1 = 4 x AAA Battery Mount
  R1 = Resistor [tolerance=±5% resistance=220 package=THT]
  R2 = Resistor [tolerance=±5% resistance=220 package=THT]
  R3 = Resistor [tolerance=±5% resistance=220 package=THT]
  R4 = Resistor [tolerance=±5% resistance=220 package=THT]
  R5 = Resistor [tolerance=±5% resistance=220 package=THT]
  R6 = Resistor [tolerance=±5% resistance=220 package=THT]

nets:
  N1: C1.-, U1.Pin_4, LED4.cathode, VCC1.-, R1.Pin_1, R2.Pin_1, R3.Pin_1, R4.Pin_0, R5.Pin_0, R6.Pin_0
  N2: C1.+, U1.Pin_8, VCC1.+
  N3: U1.Pin_1, LED4.anode
  N4: U1.Pin_2, LED3.anode
  N5: U1.Pin_3, LED5.anode
  N6: U1.Pin_5, LED2.anode
  N7: U1.Pin_6, LED7.anode
  N8: U1.Pin_7, LED6.anode

notes:
  10µ capacitor
  220Ω resistances
  3 AAA batteries (not 4 as shown in the diagram)
