# Fritzing sketch luces_tren (saved by Fritzing 0.8.7b)
breadboards: 1

parts:
  LED1 = RGB LED - (4 legs) [package="5 mm [THT]"]
  LED2 = RGB LED - (4 legs) [package="5 mm [THT]"]
  LED3 = RGB LED - (4 legs) [package="5 mm [THT]"]
  C1 = Electrolytic Capacitor [capacitance=10μF package="0605 [SMD, electrolytic]"]
  R1 = Resistor [tolerance=±5% resistance=150 package="1206 [SMD]"]
  R2 = Resistor [tolerance=±5% resistance=150 package="1206 [SMD]"]
  R3 = Resistor [tolerance=±5% resistance=150 package="1206 [SMD]"]
  R4 = Resistor [tolerance=±5% resistance=220 package="1206 [SMD]"]
  R5 = Resistor [tolerance=±5% resistance=220 package="1206 [SMD]"]
  R6 = Resistor [tolerance=±5% resistance=220 package="1206 [SMD]"]
  R7 = Resistor [tolerance=±5% resistance=220 package="1206 [SMD]"]
  R8 = Resistor [tolerance=±5% resistance=220 package="1206 [SMD]"]
  R9 = Resistor [tolerance=±5% resistance=220 package="1206 [SMD]"]
  IC2 = IC, DIP package, 14 pins [chip_label=ATTINY44/84 spacing=300mil]
  VCC1 = 4 x AAA Battery Mount

nets:
  N1: LED1.red_cathode, R6.Pin_0
  N2: LED1.common_anode, R7.Pin_0
  N3: LED1.green_cathode, LED2.green_cathode, LED3.green_cathode, C1.-, IC2.pin14, VCC1.-
  N4: LED1.blue_cathode, R2.Pin_1
  N5: LED2.red_cathode, R4.Pin_0
  N6: LED2.common_anode, R5.Pin_0
  N7: LED2.blue_cathode, R3.Pin_1
  N8: LED3.red_cathode, R8.Pin_0
  N9: LED3.common_anode, R9.Pin_0
  N10: LED3.blue_cathode, R1.Pin_1
  N11: C1.+, IC2.pin1, VCC1.+
  N12: R1.Pin_0, IC2.pin5
  N13: R2.Pin_0, IC2.pin13
  N14: R3.Pin_0, IC2.pin10
  N15: R4.Pin_1, IC2.pin8
  N16: R5.Pin_1, IC2.pin9
  N17: R6.Pin_1, IC2.pin11
  N18: R7.Pin_1, IC2.pin12
  N19: R8.Pin_1, IC2.pin3
  N20: R9.Pin_1, IC2.pin2

notes:
  AtTiny84
  R1 = 150Ω
  R2 = 220Ω
