# Fritzing sketch penales (saved by Fritzing 0.8.7b)
breadboards: 1

parts:
  Part1 = Arduino Uno (Rev3)
  VCC2 = 4 x AAA Battery Mount
  C1 = Electrolytic Capacitor [capacitance=100µF package="200 mil [THT, electrolytic]"]
  M1 = DC Motor
  IC2 = L293D [package=THT]
  J2 = Basic Servo
  C2 = Electrolytic Capacitor [capacitance=1μF package="0405 [SMD, electrolytic]"]
  R1 = Resistor [tolerance=±5% resistance=10k package=THT]
  R2 = Rotary Potentiometer (Small) [maximum_resistance=100kΩ package=THT]
  U1 = SWITCH_SPDT [package=kps-1290]
  J1 = Basic Servo
  C3 = Electrolytic Capacitor [capacitance=1μF package="0405 [SMD, electrolytic]"]
  J3 = Basic Servo
  VCC3 = 4 x AAA Battery Mount

nets:
  N1: Part1.A0, R2.wiper
  N2: Part1.D9_PWM, J3.pulse
  N3: Part1.D10_PWM/SS, J2.pulse
  N4: Part1.D11_PWM/MOSI, J1.pulse
  N5: Part1.D2, R1.Pin_0, U1.S
  N6: Part1.D3_PWM, IC2.In_2
  N7: Part1.D4, IC2.In_1
  N8: Part1.D6_PWM, IC2.Enable_1
  5V: Part1.5V, C1.+, IC2.+V, R1.Pin_1, R2.leg2, J3.vcc
  GND: Part1.GND, VCC2.-, C1.-, IC2.0V, J2.gnd, C2.-, R2.leg1, U1.O, J1.gnd, C3.-, J3.gnd, VCC3.-
  VCC: VCC2.+, J2.vcc, C2.+, J1.vcc
  N9: M1.pin_1, IC2.Out_1_(_Controlled_by_Enable_1_)
  N10: M1.pin_2, IC2.Out_2_(_Controlled_by_Enable_1_)
  N11: IC2.+Vmotor, C3.+, VCC3.+

notes:
  Al control
  Servos mov. vertical
  Servo mov.
  rotación
  Motoreductor
  mov. horizontal
