# Fritzing sketch reloko_wiring (saved by Fritzing 0.9.1b)
perfboards: 1

parts:
  C1 = Electrolytic Capacitor [capacitance=0.1mF voltage=35V package="1010 [SMD, electrolytic]"]  # not connected
  U2 = microSD Socket [package="Molex 502774-0891 [SMD]"]
  Part5 = Real Time Clock Module - DS1307 RTC Breakout Board
  Wiring1 = Wiring S [part_number="Wiring S"]
  Part1 = DeuLigne 1.1 - The Snootlab's LCD shield for Arduino
  SP1 = SPEAKER [package=pcb_mount_speaker]  # not connected
  Q1 = NPN-Transistor [package="SOT-23 [SMD]"]  # not connected
  R1 = Resistor [tolerance=±5% resistance=100 package="1206 [SMD]"]  # not connected
  C2 = Electrolytic Capacitor [capacitance=0.2µF package="100 mil [THT, electrolytic]"]  # not connected

nets:
  N1: U2.CS, Wiring1.D20
  N2: U2.DI, Wiring1.D21
  N3: U2.SCK, Wiring1.D23
  N4: U2.DO, Wiring1.D22
  5V: Part5.5V, Wiring1.3.3V
  N5: Part5.GND, Part5.SQW
  N6: Part5.SCL, Wiring1.D8
  N7: Part5.SDA, Wiring1.D9
  N8: Wiring1.D10, Part1.D8
  N9: Wiring1.D11, Part1.D9
  N10: Wiring1.D12, Part1.D4
  N11: Wiring1.D13, Part1.D5
  N12: Wiring1.D14, Part1.D6
  N13: Wiring1.D15, Part1.D7
  N14: Wiring1.D24, Part1.A0
  N15: Wiring1.GND#36, Part1.GND
  N16: Wiring1.5V#38, Part1.+5V

notes:
  8Ω, 0.5W
  100µF
  100Ω
  DS3231
  MicroSD
  0.22µF
  (Try also from PIN to VCC)
